// Logisim project AVR.circ as structural Verilog
module CORE (
  input  in_1,
  input  in_2,
  input  in_3
);

  wire [4:0] instr_reg_1_rd_out, instr_reg_1_rr_out;
  wire [7:0] alu_1_out_4, instr_reg_1__8_bit_im_out, or_1_out, registerfile_1_rd_out, registerfile_1_rr_out;
  wire [15:0] flash_1_data_out, instr_reg_1_out_15, progcounter_1_pc_out, registerfile_1_indirect_out;
  wire [31:0] decoder_1_con1;

  Clock clock_1 ();  // open: out
  Decoder decoder_1 (.in_1(instr_reg_1_out_15), .CON1(decoder_1_con1));
  FLASH flash_1 (.PC_IN(progcounter_1_pc_out), .Indirect_IN(registerfile_1_indirect_out), .DATA_OUT(flash_1_data_out));
  Instr_Reg instr_reg_1 (
    .Rd_OUT(instr_reg_1_rd_out), ._8_Bit_Im_OUT(instr_reg_1__8_bit_im_out), .in_1(flash_1_data_out),
    .out_15(instr_reg_1_out_15), .Rd_16_31(decoder_1_con1[0]), .Rd_0_31(in_3), .Rr_0_31(in_3),
    .Rd_24_26_28_30(in_3), .Bits_hnb(in_3), .Bits_lnb(in_3), .Branch_Dest(in_3), .Instr(in_3),
    .IO_0_31(in_3), ._8_Bit_Im(decoder_1_con1[1]), .Rr_OUT(instr_reg_1_rr_out));  // open: Bits_lnb_OUT, Bits_hnb_OUT, Rr_0_31_OUT, Instr_OUT, Rd_24_26_28_30_OUT
  ProgCounter progcounter_1 (
    .PC_OUT(progcounter_1_pc_out), .Indirect_IN(registerfile_1_indirect_out), .Addr_In(or_1_out),
    .LD_LO(1'b0), .LD_HI(1'b0), .PC_Enable(in_1), .RESET(in_2), .Indirect_Load(1'b0));
  ALU alu_1 (.Rd(registerfile_1_rd_out), .Rr(registerfile_1_rr_out), .out_4(alu_1_out_4), .in_1(decoder_1_con1[8:5]));
  RegisterFile registerfile_1 (
    .Indirect_OUT(registerfile_1_indirect_out), .Rd_IN(or_1_out), .WORD(decoder_1_con1[4]),
    .Rd(instr_reg_1_rd_out), .Rd_En(decoder_1_con1[2]), .Rr_En(decoder_1_con1[3]), .Rr(instr_reg_1_rr_out),
    .Rd_OUT(registerfile_1_rd_out), .Rr_OUT(registerfile_1_rr_out));
  assign or_1_out = alu_1_out_4 | instr_reg_1__8_bit_im_out;  // OR_Gate or_1, 8 bits wide
  // Probe on registerfile_1_rd_out
endmodule

module ALU (
  input  [3:0] in_1,
  input  [7:0] Rd,
  input  [7:0] Rr,
  output [7:0] out_4
);

  wire adder_1_flags_enable_2, and_1_flags_enable_2, clock_1_out, com_1_flags_enable_2, decoder_1_out1,
       decoder_1_out2, decoder_1_out3, decoder_1_out4, decoder_1_out5, decoder_1_out6, decoder_1_out7,
       decoder_1_out8, decoder_1_out9, decoder_1_out10, decoder_1_out11, decoder_1_out12, decoder_1_out13,
       decoder_1_out14, eor_1_flags_enable_2, neg_1_flags_enable_2, or_1_flags_enable_2,
       shift_1_flags_enable_2, subtractor_1_flags_enable_2;
  wire [7:0] adder_1_flags_out, and_1_data_bus_out, and_1_flags_out, com_1_data_bus_out, com_1_flags_out,
       eor_1_data_bus_out, eor_1_flags_out, neg_1_data_bus_out, neg_1_flags_out, or_1_data_bus_out,
       or_1_flags_out, shift_1_data_bus_out, shift_1_flags_out, SREG_q, subtractor_1_data_bus_out,
       subtractor_1_flags_out;

  Register #(.trigger("falling")) SREG (
    .D(adder_1_flags_out), .en(adder_1_flags_enable_2), .Q(SREG_q), .clk(clock_1_out));  // open: clr
  Clock clock_1 (.out(clock_1_out));
  // Probe on adder_1_flags_out
  ADDER adder_1 (
    .Rd(Rd), .Rr(Rr), .DATA_BUS_OUT(out_4), .DATA_BUS_IN(and_1_data_bus_out), .ADD(decoder_1_out1),
    .ADC(decoder_1_out2), .FLAGS_IN(and_1_flags_out), .FLAGS_OUT(adder_1_flags_out),
    .FLAGS_ENABLE_2(adder_1_flags_enable_2), .FLAGS_ENABLE(and_1_flags_enable_2));
  AND and_1 (
    .FLAGS_OUT(and_1_flags_out), .FLAGS_ENABLE_2(and_1_flags_enable_2), .DATA_BUS_OUT(and_1_data_bus_out),
    .AND(decoder_1_out3), .FLAGS_IN(shift_1_flags_out), .FLAGS_ENABLE(shift_1_flags_enable_2),
    .DATA_BUS_IN(shift_1_data_bus_out), .Rd(Rd), .Rr(Rr));
  SHIFT shift_1 (
    .Rd(Rd), .FLAGS_OUT(shift_1_flags_out), .FLAGS_ENABLE_2(shift_1_flags_enable_2),
    .DATA_BUS_OUT(shift_1_data_bus_out), .LSL(decoder_1_out4), .FLAGS_IN(subtractor_1_flags_out),
    .FLAGS_ENABLE(subtractor_1_flags_enable_2), .DATA_BUS_IN(subtractor_1_data_bus_out),
    .LSR(decoder_1_out5), .ROL(decoder_1_out6), .ROR(decoder_1_out7), .ASR(decoder_1_out8));
  SUBTRACTOR subtractor_1 (
    .FLAGS_OUT(subtractor_1_flags_out), .FLAGS_ENABLE_2(subtractor_1_flags_enable_2),
    .DATA_BUS_OUT(subtractor_1_data_bus_out), .Rd(Rd), .Rr(Rr), .SUB(decoder_1_out9), .SBC(decoder_1_out10),
    .FLAGS_IN(or_1_flags_out), .FLAGS_ENABLE(or_1_flags_enable_2), .DATA_BUS_IN(or_1_data_bus_out));
  OR or_1 (
    .FLAGS_OUT(or_1_flags_out), .FLAGS_ENABLE_2(or_1_flags_enable_2), .DATA_BUS_OUT(or_1_data_bus_out),
    .Rd(Rd), .OR(decoder_1_out11), .Rr(Rr), .FLAGS_IN(eor_1_flags_out), .FLAGS_ENABLE(eor_1_flags_enable_2),
    .DATA_BUS_IN(eor_1_data_bus_out));
  EOR eor_1 (
    .Rd(Rd), .Rr(Rr), .EOR(decoder_1_out12), .FLAGS_OUT(eor_1_flags_out),
    .FLAGS_ENABLE_2(eor_1_flags_enable_2), .DATA_BUS_OUT(eor_1_data_bus_out), .FLAGS_IN(com_1_flags_out),
    .FLAGS_ENABLE(com_1_flags_enable_2), .DATA_BUS_IN(com_1_data_bus_out));
  COM com_1 (
    .Rd(Rd), .COM(decoder_1_out13), .FLAGS_OUT(com_1_flags_out), .FLAGS_ENABLE_2(com_1_flags_enable_2),
    .DATA_BUS_OUT(com_1_data_bus_out), .FLAGS_IN(neg_1_flags_out), .FLAGS_ENABLE(neg_1_flags_enable_2),
    .DATA_BUS_IN(neg_1_data_bus_out));
  NEG neg_1 (
    .Rd(Rd), .COM(decoder_1_out14), .FLAGS_OUT(neg_1_flags_out), .FLAGS_ENABLE_2(neg_1_flags_enable_2),
    .DATA_BUS_OUT(neg_1_data_bus_out), .FLAGS_IN(SREG_q), .FLAGS_ENABLE(1'b0), .DATA_BUS_IN({8{1'b0}}));
  Decoder_part #(.select(4)) decoder_1 (
    .out1(decoder_1_out1), .out2(decoder_1_out2), .out3(decoder_1_out3), .out4(decoder_1_out4),
    .out5(decoder_1_out5), .out6(decoder_1_out6), .out7(decoder_1_out7), .out8(decoder_1_out8),
    .out9(decoder_1_out9), .out10(decoder_1_out10), .out11(decoder_1_out11), .out12(decoder_1_out12),
    .out13(decoder_1_out13), .out14(decoder_1_out14), .sel(in_1), .en(1'b1));  // open: out0, out15
endmodule

// ADD
module ADDER (
  input  [7:0] Rd,
  input  [7:0] Rr,
  input  ADD,
  input  ADC,
  input  [7:0] FLAGS_IN,
  input  FLAGS_ENABLE,
  input  [7:0] DATA_BUS_IN,
  output [7:0] FLAGS_OUT,
  output FLAGS_ENABLE_2,
  output [7:0] DATA_BUS_OUT
);

  wire adder_1_cout, adder_2_cout, and_1_out, and_2_out, comparator_1_eq, controlled_buffer_7_out, not_4_out,
       or_1_out, or_4_out, xor_1_out;
  wire [3:0] not_2_out, not_3_out;
  wire [7:0] adder_1_out, not_1_out, pull_resistor_1_node;

  assign not_1_out = ~adder_1_out;  // NOT_Gate not_1, 8 bits wide
  and and_1 (and_1_out, Rd[7], Rr[7], not_1_out[7]);
  or or_1 (or_1_out, and_1_out, and_2_out);
  assign not_2_out = ~Rr[7:4];  // NOT_Gate not_2, 4 bits wide
  assign not_3_out = ~Rd[7:4];  // NOT_Gate not_3, 4 bits wide
  and and_2 (and_2_out, not_3_out[3], not_2_out[3], adder_1_out[7]);
  Adder #(.width(4)) adder_1 (
    .a(Rd[3:0]), .b(Rr[3:0]), .out(adder_1_out[3:0]), .cin(controlled_buffer_7_out), .cout(adder_1_cout));
  Adder #(.width(4)) adder_2 (
    .a(Rd[7:4]), .b(Rr[7:4]), .out(adder_1_out[7:4]), .cin(adder_1_cout), .cout(adder_2_cout));
  assign FLAGS_OUT[0] = or_4_out ? adder_2_cout : 1'bz;  // Controlled_Buffer controlled_buffer_1
  assign FLAGS_OUT[1] = or_4_out ? comparator_1_eq : 1'bz;  // Controlled_Buffer controlled_buffer_2
  assign FLAGS_OUT[2] = or_4_out ? adder_1_out[7] : 1'bz;  // Controlled_Buffer controlled_buffer_3
  assign FLAGS_OUT[3] = or_4_out ? or_1_out : 1'bz;  // Controlled_Buffer controlled_buffer_4
  assign FLAGS_OUT[4] = or_4_out ? xor_1_out : 1'bz;  // Controlled_Buffer controlled_buffer_5
  xor xor_1 (xor_1_out, FLAGS_OUT[3], FLAGS_OUT[2]);
  assign FLAGS_OUT[5] = or_4_out ? adder_1_cout : 1'bz;  // Controlled_Buffer controlled_buffer_6
  assign controlled_buffer_7_out = ADC ? FLAGS_IN[0] : 1'bz;  // Controlled_Buffer controlled_buffer_7
  Comparator comparator_1 (.a(adder_1_out), .b({8{1'b0}}), .eq(comparator_1_eq));  // open: gt, lt
  assign FLAGS_OUT[2] = not_4_out ? FLAGS_IN[2] : 1'bz;  // Controlled_Buffer controlled_buffer_8
  assign FLAGS_OUT[5] = not_4_out ? FLAGS_IN[5] : 1'bz;  // Controlled_Buffer controlled_buffer_9
  assign FLAGS_OUT[4] = not_4_out ? FLAGS_IN[4] : 1'bz;  // Controlled_Buffer controlled_buffer_10
  assign FLAGS_OUT[1] = not_4_out ? FLAGS_IN[1] : 1'bz;  // Controlled_Buffer controlled_buffer_11
  assign FLAGS_OUT[3] = not_4_out ? FLAGS_IN[3] : 1'bz;  // Controlled_Buffer controlled_buffer_12
  assign FLAGS_OUT[0] = not_4_out ? FLAGS_IN[0] : 1'bz;  // Controlled_Buffer controlled_buffer_13
  or or_2 (FLAGS_ENABLE_2, FLAGS_ENABLE, or_4_out);
  not not_4 (not_4_out, or_4_out);
  assign DATA_BUS_OUT = pull_resistor_1_node | DATA_BUS_IN;  // OR_Gate or_3, 8 bits wide
  Pull_Resistor pull_resistor_1 (.node(pull_resistor_1_node));
  assign pull_resistor_1_node = or_4_out ? adder_1_out : 8'bz;  // Controlled_Buffer controlled_buffer_14
  or or_4 (or_4_out, ADC, ADD);

  assign FLAGS_OUT[7:6] = FLAGS_IN[7:6];
endmodule

module AND (
  input  [7:0] Rd,
  input  AND,
  input  [7:0] Rr,
  input  [7:0] FLAGS_IN,
  input  FLAGS_ENABLE,
  input  [7:0] DATA_BUS_IN,
  output [7:0] FLAGS_OUT,
  output FLAGS_ENABLE_2,
  output [7:0] DATA_BUS_OUT
);

  wire comparator_1_eq, not_1_out, xor_1_out;
  wire [7:0] and_1_out, pull_resistor_2_node;

  assign and_1_out = Rd & Rr;  // AND_Gate and_1, 8 bits wide
  assign FLAGS_OUT[2] = AND ? and_1_out[7] : 1'bz;  // Controlled_Buffer controlled_buffer_1
  xor xor_1 (xor_1_out, and_1_out[7], FLAGS_OUT[3]);
  assign FLAGS_OUT[4] = AND ? xor_1_out : 1'bz;  // Controlled_Buffer controlled_buffer_2
  assign FLAGS_OUT[4] = not_1_out ? FLAGS_IN[4] : 1'bz;  // Controlled_Buffer controlled_buffer_3
  Comparator comparator_1 (.a(and_1_out), .b({8{1'b0}}), .eq(comparator_1_eq));  // open: gt, lt
  Pull_Resistor pull_resistor_1 (.node(FLAGS_OUT[3]));
  assign FLAGS_OUT[3] = not_1_out ? FLAGS_IN[3] : 1'bz;  // Controlled_Buffer controlled_buffer_4
  assign FLAGS_OUT[1] = not_1_out ? FLAGS_IN[1] : 1'bz;  // Controlled_Buffer controlled_buffer_5
  assign FLAGS_OUT[2] = not_1_out ? FLAGS_IN[2] : 1'bz;  // Controlled_Buffer controlled_buffer_6
  or or_1 (FLAGS_ENABLE_2, FLAGS_ENABLE, AND);
  assign FLAGS_OUT[1] = AND ? comparator_1_eq : 1'bz;  // Controlled_Buffer controlled_buffer_7
  not not_1 (not_1_out, AND);
  assign DATA_BUS_OUT = pull_resistor_2_node | DATA_BUS_IN;  // OR_Gate or_2, 8 bits wide
  Pull_Resistor pull_resistor_2 (.node(pull_resistor_2_node));
  assign pull_resistor_2_node = AND ? and_1_out : 8'bz;  // Controlled_Buffer controlled_buffer_8

  assign {FLAGS_OUT[7:5], FLAGS_OUT[0]} = {FLAGS_IN[7:5], FLAGS_IN[0]};
endmodule

module SHIFT (
  input  LSL,
  input  LSR,
  input  [7:0] Rd,
  input  ROL,
  input  ROR,
  input  ASR,
  input  [7:0] FLAGS_IN,
  input  FLAGS_ENABLE,
  input  [7:0] DATA_BUS_IN,
  output [7:0] FLAGS_OUT,
  output FLAGS_ENABLE_2,
  output [7:0] DATA_BUS_OUT
);

  wire comparator_1_eq, not_1_out, not_2_out, not_3_out, or_2_out, or_4_out, xor_1_out, xor_2_out;
  wire [6:0] controlled_buffer_1_out, controlled_buffer_3_out, controlled_buffer_6_out;
  wire [7:0] pull_resistor_1_node;
  wire [7:1] controlled_buffer_2_out, controlled_buffer_4_out, controlled_buffer_5_out;

  assign {FLAGS_OUT[0], controlled_buffer_1_out[6:5], FLAGS_OUT[5], controlled_buffer_1_out[3:0]} = LSL ? Rd : 8'bz;  // Controlled_Buffer controlled_buffer_1
  assign {controlled_buffer_2_out, FLAGS_OUT[0]} = LSR ? Rd : 8'bz;  // Controlled_Buffer controlled_buffer_2
  assign {FLAGS_OUT[0], controlled_buffer_3_out[6:4], FLAGS_OUT[5], controlled_buffer_3_out[2:0]} = ROL ? Rd : 8'bz;  // Controlled_Buffer controlled_buffer_3
  assign {controlled_buffer_4_out, FLAGS_OUT[0]} = ROR ? Rd : 8'bz;  // Controlled_Buffer controlled_buffer_4
  assign {controlled_buffer_5_out, FLAGS_OUT[0]} = ASR ? Rd : 8'bz;  // Controlled_Buffer controlled_buffer_5
  assign {FLAGS_OUT[2], controlled_buffer_6_out} = LSL ? {controlled_buffer_1_out[6:5], FLAGS_OUT[5], controlled_buffer_1_out[3:0], 1'b0} : 8'bz;  // Controlled_Buffer controlled_buffer_6
  assign {FLAGS_OUT[2], controlled_buffer_6_out} = LSR ? {1'b0, controlled_buffer_2_out} : 8'bz;  // Controlled_Buffer controlled_buffer_7
  assign {FLAGS_OUT[2], controlled_buffer_6_out} = ROL ? {controlled_buffer_3_out[6:4], FLAGS_OUT[5], controlled_buffer_3_out[2:0], FLAGS_IN[0]} : 8'bz;  // Controlled_Buffer controlled_buffer_8
  assign {FLAGS_OUT[2], controlled_buffer_6_out} = ROR ? {FLAGS_IN[0], controlled_buffer_4_out} : 8'bz;  // Controlled_Buffer controlled_buffer_9
  assign {FLAGS_OUT[2], controlled_buffer_6_out} = ASR ? {controlled_buffer_5_out[7], 1'b0, controlled_buffer_5_out[6:1]} : 8'bz;  // Controlled_Buffer controlled_buffer_10
  Comparator comparator_1 (
    .a({FLAGS_OUT[2], controlled_buffer_6_out}), .b({8{1'b0}}), .eq(comparator_1_eq));  // open: gt, lt
  xor xor_1 (xor_1_out, FLAGS_OUT[0], FLAGS_OUT[2]);
  assign FLAGS_OUT[3] = or_4_out ? xor_1_out : 1'bz;  // Controlled_Buffer controlled_buffer_11
  assign FLAGS_OUT[4] = or_4_out ? xor_2_out : 1'bz;  // Controlled_Buffer controlled_buffer_12
  xor xor_2 (xor_2_out, FLAGS_OUT[2], FLAGS_OUT[3]);
  assign FLAGS_OUT[1] = or_4_out ? comparator_1_eq : 1'bz;  // Controlled_Buffer controlled_buffer_13
  assign FLAGS_OUT[2] = LSR ? not_2_out : 1'bz;  // Controlled_Buffer controlled_buffer_14
  assign FLAGS_OUT[5] = not_1_out ? FLAGS_IN[5] : 1'bz;  // Controlled_Buffer controlled_buffer_15
  not not_1 (not_1_out, or_2_out);
  assign FLAGS_OUT[1] = not_3_out ? FLAGS_IN[1] : 1'bz;  // Controlled_Buffer controlled_buffer_16
  assign FLAGS_OUT[4] = not_3_out ? FLAGS_IN[4] : 1'bz;  // Controlled_Buffer controlled_buffer_17
  assign FLAGS_OUT[2] = not_3_out ? FLAGS_IN[2] : 1'bz;  // Controlled_Buffer controlled_buffer_18
  assign FLAGS_OUT[3] = not_3_out ? FLAGS_IN[3] : 1'bz;  // Controlled_Buffer controlled_buffer_19
  assign FLAGS_OUT[0] = not_3_out ? FLAGS_IN[0] : 1'bz;  // Controlled_Buffer controlled_buffer_20
  or or_1 (FLAGS_ENABLE_2, FLAGS_ENABLE, or_4_out);
  not not_2 (not_2_out, LSR);
  or or_2 (or_2_out, LSL, ROL);
  assign DATA_BUS_OUT = pull_resistor_1_node | DATA_BUS_IN;  // OR_Gate or_3, 8 bits wide
  Pull_Resistor pull_resistor_1 (.node(pull_resistor_1_node));
  assign pull_resistor_1_node = or_4_out ? {FLAGS_OUT[2], controlled_buffer_6_out} : 8'bz;  // Controlled_Buffer controlled_buffer_21
  not not_3 (not_3_out, or_4_out);
  or or_4 (or_4_out, LSL, LSR, ROL, ROR, ASR);

  assign FLAGS_OUT[7:6] = FLAGS_IN[7:6];
endmodule

// SUB
module SUBTRACTOR (
  input  [7:0] Rd,
  input  [7:0] Rr,
  input  SUB,
  input  SBC,
  input  [7:0] FLAGS_IN,
  input  FLAGS_ENABLE,
  input  [7:0] DATA_BUS_IN,
  output [7:0] FLAGS_OUT,
  output FLAGS_ENABLE_2,
  output [7:0] DATA_BUS_OUT
);

  wire and_1_out, and_2_out, comparator_1_eq, controlled_buffer_7_out, not_4_out, or_1_out, or_4_out,
       subtractor_1_bout, subtractor_2_bout, xor_1_out;
  wire [3:0] not_2_out, not_3_out, subtractor_1_out, subtractor_2_out;
  wire [7:0] not_1_out, pull_resistor_1_node;

  assign not_1_out = ~{subtractor_2_out, subtractor_1_out};  // NOT_Gate not_1, 8 bits wide
  assign not_2_out = ~Rr[7:4];  // NOT_Gate not_2, 4 bits wide
  and and_1 (and_1_out, Rd[7], not_2_out[3], not_1_out[7]);
  or or_1 (or_1_out, and_1_out, and_2_out);
  assign not_3_out = ~Rd[7:4];  // NOT_Gate not_3, 4 bits wide
  and and_2 (and_2_out, not_3_out[3], Rr[7], subtractor_2_out[3]);
  Subtractor #(.width(4)) subtractor_1 (
    .a(Rd[3:0]), .b(Rr[3:0]), .out(subtractor_1_out), .bin(controlled_buffer_7_out), .bout(subtractor_1_bout));
  Subtractor #(.width(4)) subtractor_2 (
    .a(Rd[7:4]), .b(Rr[7:4]), .out(subtractor_2_out), .bin(subtractor_1_bout), .bout(subtractor_2_bout));
  assign FLAGS_OUT[0] = or_4_out ? subtractor_2_bout : 1'bz;  // Controlled_Buffer controlled_buffer_1
  assign FLAGS_OUT[1] = or_4_out ? comparator_1_eq : 1'bz;  // Controlled_Buffer controlled_buffer_2
  assign FLAGS_OUT[2] = or_4_out ? subtractor_2_out[3] : 1'bz;  // Controlled_Buffer controlled_buffer_3
  assign FLAGS_OUT[3] = or_4_out ? or_1_out : 1'bz;  // Controlled_Buffer controlled_buffer_4
  assign FLAGS_OUT[4] = or_4_out ? xor_1_out : 1'bz;  // Controlled_Buffer controlled_buffer_5
  xor xor_1 (xor_1_out, FLAGS_OUT[3], FLAGS_OUT[2]);
  assign FLAGS_OUT[5] = or_4_out ? subtractor_1_bout : 1'bz;  // Controlled_Buffer controlled_buffer_6
  assign controlled_buffer_7_out = SBC ? FLAGS_IN[0] : 1'bz;  // Controlled_Buffer controlled_buffer_7
  Comparator comparator_1 (
    .a({subtractor_2_out, subtractor_1_out}), .b({8{1'b0}}), .eq(comparator_1_eq));  // open: gt, lt
  assign FLAGS_OUT[4] = not_4_out ? FLAGS_IN[4] : 1'bz;  // Controlled_Buffer controlled_buffer_8
  assign FLAGS_OUT[5] = not_4_out ? FLAGS_IN[5] : 1'bz;  // Controlled_Buffer controlled_buffer_9
  assign FLAGS_OUT[3] = not_4_out ? FLAGS_IN[3] : 1'bz;  // Controlled_Buffer controlled_buffer_10
  assign FLAGS_OUT[2] = not_4_out ? FLAGS_IN[2] : 1'bz;  // Controlled_Buffer controlled_buffer_11
  assign FLAGS_OUT[1] = not_4_out ? FLAGS_IN[1] : 1'bz;  // Controlled_Buffer controlled_buffer_12
  assign FLAGS_OUT[0] = not_4_out ? FLAGS_IN[0] : 1'bz;  // Controlled_Buffer controlled_buffer_13
  or or_2 (FLAGS_ENABLE_2, FLAGS_ENABLE, or_4_out);
  not not_4 (not_4_out, or_4_out);
  assign DATA_BUS_OUT = pull_resistor_1_node | DATA_BUS_IN;  // OR_Gate or_3, 8 bits wide
  Pull_Resistor pull_resistor_1 (.node(pull_resistor_1_node));
  assign pull_resistor_1_node = or_4_out ? {subtractor_2_out, subtractor_1_out} : 8'bz;  // Controlled_Buffer controlled_buffer_14
  or or_4 (or_4_out, SBC, SUB);

  assign FLAGS_OUT[7:6] = FLAGS_IN[7:6];
endmodule

module OR (
  input  [7:0] Rd,
  input  OR,
  input  [7:0] Rr,
  input  [7:0] FLAGS_IN,
  input  FLAGS_ENABLE,
  input  [7:0] DATA_BUS_IN,
  output [7:0] FLAGS_OUT,
  output FLAGS_ENABLE_2,
  output [7:0] DATA_BUS_OUT
);

  wire comparator_1_eq, not_1_out, xor_1_out;
  wire [7:0] or_1_out, pull_resistor_2_node;

  assign or_1_out = Rd | Rr;  // OR_Gate or_1, 8 bits wide
  assign FLAGS_OUT[2] = OR ? or_1_out[7] : 1'bz;  // Controlled_Buffer controlled_buffer_1
  assign FLAGS_OUT[4] = OR ? xor_1_out : 1'bz;  // Controlled_Buffer controlled_buffer_2
  xor xor_1 (xor_1_out, or_1_out[7], FLAGS_OUT[3]);
  assign FLAGS_OUT[4] = not_1_out ? FLAGS_IN[4] : 1'bz;  // Controlled_Buffer controlled_buffer_3
  Comparator comparator_1 (.a(or_1_out), .b({8{1'b0}}), .eq(comparator_1_eq));  // open: gt, lt
  Pull_Resistor pull_resistor_1 (.node(FLAGS_OUT[3]));
  assign FLAGS_OUT[2] = not_1_out ? FLAGS_IN[2] : 1'bz;  // Controlled_Buffer controlled_buffer_4
  assign FLAGS_OUT[1] = not_1_out ? FLAGS_IN[1] : 1'bz;  // Controlled_Buffer controlled_buffer_5
  assign FLAGS_OUT[3] = not_1_out ? FLAGS_IN[3] : 1'bz;  // Controlled_Buffer controlled_buffer_6
  or or_2 (FLAGS_ENABLE_2, FLAGS_ENABLE, OR);
  assign FLAGS_OUT[1] = OR ? comparator_1_eq : 1'bz;  // Controlled_Buffer controlled_buffer_7
  not not_1 (not_1_out, OR);
  assign DATA_BUS_OUT = pull_resistor_2_node | DATA_BUS_IN;  // OR_Gate or_3, 8 bits wide
  Pull_Resistor pull_resistor_2 (.node(pull_resistor_2_node));
  assign pull_resistor_2_node = OR ? or_1_out : 8'bz;  // Controlled_Buffer controlled_buffer_8

  assign {FLAGS_OUT[7:5], FLAGS_OUT[0]} = {FLAGS_IN[7:5], FLAGS_IN[0]};
endmodule

module EOR (
  input  [7:0] Rd,
  input  EOR,
  input  [7:0] Rr,
  input  [7:0] FLAGS_IN,
  input  FLAGS_ENABLE,
  input  [7:0] DATA_BUS_IN,
  output [7:0] FLAGS_OUT,
  output FLAGS_ENABLE_2,
  output [7:0] DATA_BUS_OUT
);

  wire comparator_1_eq, not_1_out, xor_2_out;
  wire [7:0] pull_resistor_2_node, xor_1_out;

  assign xor_1_out = Rd ^ Rr;  // XOR_Gate xor_1, 8 bits wide
  assign FLAGS_OUT[2] = EOR ? xor_1_out[7] : 1'bz;  // Controlled_Buffer controlled_buffer_1
  xor xor_2 (xor_2_out, xor_1_out[7], FLAGS_OUT[3]);
  assign FLAGS_OUT[4] = EOR ? xor_2_out : 1'bz;  // Controlled_Buffer controlled_buffer_2
  assign FLAGS_OUT[4] = not_1_out ? FLAGS_IN[4] : 1'bz;  // Controlled_Buffer controlled_buffer_3
  Comparator comparator_1 (.a(xor_1_out), .b({8{1'b0}}), .eq(comparator_1_eq));  // open: gt, lt
  Pull_Resistor pull_resistor_1 (.node(FLAGS_OUT[3]));
  assign FLAGS_OUT[2] = not_1_out ? FLAGS_IN[2] : 1'bz;  // Controlled_Buffer controlled_buffer_4
  assign FLAGS_OUT[1] = not_1_out ? FLAGS_IN[1] : 1'bz;  // Controlled_Buffer controlled_buffer_5
  assign FLAGS_OUT[3] = not_1_out ? FLAGS_IN[3] : 1'bz;  // Controlled_Buffer controlled_buffer_6
  or or_1 (FLAGS_ENABLE_2, FLAGS_ENABLE, EOR);
  assign FLAGS_OUT[1] = EOR ? comparator_1_eq : 1'bz;  // Controlled_Buffer controlled_buffer_7
  not not_1 (not_1_out, EOR);
  assign DATA_BUS_OUT = pull_resistor_2_node | DATA_BUS_IN;  // OR_Gate or_2, 8 bits wide
  Pull_Resistor pull_resistor_2 (.node(pull_resistor_2_node));
  assign pull_resistor_2_node = EOR ? xor_1_out : 8'bz;  // Controlled_Buffer controlled_buffer_8

  assign {FLAGS_OUT[7:5], FLAGS_OUT[0]} = {FLAGS_IN[7:5], FLAGS_IN[0]};
endmodule

module COM (
  input  [7:0] Rd,
  input  COM,
  input  [7:0] FLAGS_IN,
  input  FLAGS_ENABLE,
  input  [7:0] DATA_BUS_IN,
  output [7:0] FLAGS_OUT,
  output FLAGS_ENABLE_2,
  output [7:0] DATA_BUS_OUT
);

  wire comparator_1_eq, not_1_out, xor_1_out;
  wire [7:0] pull_resistor_3_node, subtractor_1_out;

  Subtractor subtractor_1 (.a({8{1'b1}}), .b(Rd), .out(subtractor_1_out));  // open: bin, bout
  assign FLAGS_OUT[2] = COM ? subtractor_1_out[7] : 1'bz;  // Controlled_Buffer controlled_buffer_1
  assign FLAGS_OUT[4] = COM ? xor_1_out : 1'bz;  // Controlled_Buffer controlled_buffer_2
  xor xor_1 (xor_1_out, subtractor_1_out[7], FLAGS_OUT[3]);
  assign FLAGS_OUT[4] = not_1_out ? FLAGS_IN[4] : 1'bz;  // Controlled_Buffer controlled_buffer_3
  Comparator comparator_1 (.a(subtractor_1_out), .b({8{1'b0}}), .eq(comparator_1_eq));  // open: gt, lt
  Pull_Resistor pull_resistor_1 (.node(FLAGS_OUT[0]));
  Pull_Resistor pull_resistor_2 (.node(FLAGS_OUT[3]));
  assign FLAGS_OUT[3] = not_1_out ? FLAGS_IN[3] : 1'bz;  // Controlled_Buffer controlled_buffer_4
  assign FLAGS_OUT[0] = not_1_out ? FLAGS_IN[0] : 1'bz;  // Controlled_Buffer controlled_buffer_5
  assign FLAGS_OUT[1] = not_1_out ? FLAGS_IN[1] : 1'bz;  // Controlled_Buffer controlled_buffer_6
  assign FLAGS_OUT[2] = not_1_out ? FLAGS_IN[2] : 1'bz;  // Controlled_Buffer controlled_buffer_7
  or or_1 (FLAGS_ENABLE_2, FLAGS_ENABLE, COM);
  assign FLAGS_OUT[1] = COM ? comparator_1_eq : 1'bz;  // Controlled_Buffer controlled_buffer_8
  not not_1 (not_1_out, COM);
  assign DATA_BUS_OUT = pull_resistor_3_node | DATA_BUS_IN;  // OR_Gate or_2, 8 bits wide
  Pull_Resistor pull_resistor_3 (.node(pull_resistor_3_node));
  assign pull_resistor_3_node = COM ? subtractor_1_out : 8'bz;  // Controlled_Buffer controlled_buffer_9

  assign FLAGS_OUT[7:5] = FLAGS_IN[7:5];
endmodule

module NEG (
  input  [7:0] Rd,
  input  COM,
  input  [7:0] FLAGS_IN,
  input  FLAGS_ENABLE,
  input  [7:0] DATA_BUS_IN,
  output [7:0] FLAGS_OUT,
  output FLAGS_ENABLE_2,
  output [7:0] DATA_BUS_OUT
);

  wire comparator_1_eq, comparator_2_eq, not_1_out, not_2_out, or_1_out, xor_1_out;
  wire [7:0] pull_resistor_1_node, subtractor_1_out;

  Subtractor subtractor_1 (.a({8{1'b0}}), .b(Rd), .out(subtractor_1_out));  // open: bin, bout
  assign FLAGS_OUT[2] = COM ? subtractor_1_out[7] : 1'bz;  // Controlled_Buffer controlled_buffer_1
  assign FLAGS_OUT[4] = COM ? xor_1_out : 1'bz;  // Controlled_Buffer controlled_buffer_2
  xor xor_1 (xor_1_out, subtractor_1_out[7], FLAGS_OUT[3]);
  or or_1 (or_1_out, subtractor_1_out[3], Rd[3]);
  assign FLAGS_OUT[5] = COM ? or_1_out : 1'bz;  // Controlled_Buffer controlled_buffer_3
  assign FLAGS_OUT[3] = COM ? comparator_1_eq : 1'bz;  // Controlled_Buffer controlled_buffer_4
  Comparator comparator_1 (.a(subtractor_1_out), .b(8'h80), .eq(comparator_1_eq));  // open: gt, lt
  Comparator comparator_2 (.a(subtractor_1_out), .b({8{1'b0}}), .eq(comparator_2_eq));  // open: gt, lt
  assign FLAGS_OUT[4] = not_2_out ? FLAGS_IN[4] : 1'bz;  // Controlled_Buffer controlled_buffer_5
  assign FLAGS_OUT[3] = not_2_out ? FLAGS_IN[3] : 1'bz;  // Controlled_Buffer controlled_buffer_6
  assign FLAGS_OUT[0] = not_2_out ? FLAGS_IN[0] : 1'bz;  // Controlled_Buffer controlled_buffer_7
  assign FLAGS_OUT[2] = not_2_out ? FLAGS_IN[2] : 1'bz;  // Controlled_Buffer controlled_buffer_8
  assign FLAGS_OUT[1] = not_2_out ? FLAGS_IN[1] : 1'bz;  // Controlled_Buffer controlled_buffer_9
  assign FLAGS_OUT[5] = not_2_out ? FLAGS_IN[5] : 1'bz;  // Controlled_Buffer controlled_buffer_10
  or or_2 (FLAGS_ENABLE_2, FLAGS_ENABLE, COM);
  assign FLAGS_OUT[1] = COM ? comparator_2_eq : 1'bz;  // Controlled_Buffer controlled_buffer_11
  not not_1 (not_1_out, comparator_2_eq);
  assign FLAGS_OUT[0] = COM ? not_1_out : 1'bz;  // Controlled_Buffer controlled_buffer_12
  not not_2 (not_2_out, COM);
  assign DATA_BUS_OUT = pull_resistor_1_node | DATA_BUS_IN;  // OR_Gate or_3, 8 bits wide
  Pull_Resistor pull_resistor_1 (.node(pull_resistor_1_node));
  assign pull_resistor_1_node = COM ? subtractor_1_out : 8'bz;  // Controlled_Buffer controlled_buffer_13

  assign FLAGS_OUT[7:6] = FLAGS_IN[7:6];
endmodule

// Registers
module RegisterFile (
  input  [7:0] Rd_IN,
  input  WORD,
  input  [4:0] Rd,
  input  Rd_En,
  input  Rr_En,
  input  [4:0] Rr,
  output [15:0] Indirect_OUT,
  output [7:0] Rd_OUT,
  output [7:0] Rr_OUT
);

  wire clock_1_out, decoder_1_out0, decoder_1_out1, decoder_1_out2, decoder_1_out3, decoder_1_out4,
       decoder_1_out5, decoder_1_out6, decoder_1_out7, decoder_1_out8, decoder_1_out9, decoder_1_out10,
       decoder_1_out11, decoder_1_out12, decoder_1_out13, decoder_1_out14, decoder_1_out15, decoder_1_out16,
       decoder_1_out17, decoder_1_out18, decoder_1_out19, decoder_1_out20, decoder_1_out21, decoder_1_out22,
       decoder_1_out23, decoder_1_out24, decoder_1_out25, decoder_1_out26, decoder_1_out27, decoder_1_out28,
       decoder_1_out29, decoder_1_out30, decoder_1_out31, decoder_2_out0, decoder_2_out1, decoder_2_out2,
       decoder_2_out3, decoder_2_out4, decoder_2_out5, decoder_2_out6, decoder_2_out7, decoder_2_out8,
       decoder_2_out9, decoder_2_out10, decoder_2_out11, decoder_2_out12, decoder_2_out13, decoder_2_out14,
       decoder_2_out15, decoder_2_out16, decoder_2_out17, decoder_2_out18, decoder_2_out19, decoder_2_out20,
       decoder_2_out21, decoder_2_out22, decoder_2_out23, decoder_2_out24, decoder_2_out25, decoder_2_out26,
       decoder_2_out27, decoder_2_out28, decoder_2_out29, decoder_2_out30, decoder_2_out31, or_2_out,
       or_4_out;
  wire [4:0] controlled_buffer_2_out, or_1_out, or_3_out;
  wire [7:0] controlled_buffer_4_out, controlled_buffer_7_out, controlled_buffer_10_out,
       controlled_buffer_13_out, controlled_buffer_16_out, controlled_buffer_19_out,
       controlled_buffer_22_out, controlled_buffer_25_out, controlled_buffer_27_out,
       controlled_buffer_28_out, controlled_buffer_29_out, controlled_buffer_30_out,
       controlled_buffer_31_out, controlled_buffer_32_out, controlled_buffer_33_out,
       controlled_buffer_34_out, controlled_buffer_36_out, controlled_buffer_39_out,
       controlled_buffer_42_out, controlled_buffer_45_out, controlled_buffer_48_out,
       controlled_buffer_51_out, controlled_buffer_54_out, controlled_buffer_57_out,
       controlled_buffer_76_out, controlled_buffer_79_out, controlled_buffer_82_out,
       controlled_buffer_85_out, controlled_buffer_88_out, controlled_buffer_91_out,
       controlled_buffer_94_out, controlled_buffer_97_out, register_1_q, register_2_q, register_3_q,
       register_4_q, register_5_q, register_6_q, register_7_q, register_8_q, register_9_q, register_10_q,
       register_11_q, register_12_q, register_13_q, register_14_q, register_15_q, register_16_q,
       register_17_q, register_18_q, register_19_q, register_20_q, register_21_q, register_22_q,
       register_23_q, register_24_q, register_25_q, register_26_q, register_27_q, register_28_q,
       register_29_q, register_30_q, register_31_q, register_32_q;

  assign or_1_out = controlled_buffer_2_out | Rr;  // OR_Gate or_1, 5 bits wide
  Decoder_part #(.select(5), .disabled(0)) decoder_1 (
    .out0(decoder_1_out0), .out1(decoder_1_out1), .out2(decoder_1_out2), .out3(decoder_1_out3),
    .out4(decoder_1_out4), .out5(decoder_1_out5), .out6(decoder_1_out6), .out7(decoder_1_out7),
    .out8(decoder_1_out8), .out9(decoder_1_out9), .out10(decoder_1_out10), .out11(decoder_1_out11),
    .out12(decoder_1_out12), .out13(decoder_1_out13), .out14(decoder_1_out14), .out15(decoder_1_out15),
    .out16(decoder_1_out16), .out17(decoder_1_out17), .out18(decoder_1_out18), .out19(decoder_1_out19),
    .out20(decoder_1_out20), .out21(decoder_1_out21), .out22(decoder_1_out22), .out23(decoder_1_out23),
    .out24(decoder_1_out24), .out25(decoder_1_out25), .out26(decoder_1_out26), .out27(decoder_1_out27),
    .out28(decoder_1_out28), .out29(decoder_1_out29), .out30(decoder_1_out30), .out31(decoder_1_out31),
    .sel(or_1_out), .en(or_2_out));
  assign Indirect_OUT = WORD ? {Rr_OUT, Rd_OUT} : 16'bz;  // Controlled_Buffer controlled_buffer_1
  Pull_Resistor pull_resistor_1 (.node(Indirect_OUT));
  // Probe on controlled_buffer_2_out
  or or_2 (or_2_out, WORD, Rr_En);
  assign or_3_out = 5'b00001 | Rd;  // OR_Gate or_3, 5 bits wide
  assign controlled_buffer_2_out = WORD ? or_3_out : 5'bz;  // Controlled_Buffer controlled_buffer_2
  Pull_Resistor pull_resistor_2 (.node(controlled_buffer_2_out));
  or or_4 (or_4_out, Rd_En, WORD);
  Decoder_part #(.select(5), .disabled(0)) decoder_2 (
    .out0(decoder_2_out0), .out1(decoder_2_out1), .out2(decoder_2_out2), .out3(decoder_2_out3),
    .out4(decoder_2_out4), .out5(decoder_2_out5), .out6(decoder_2_out6), .out7(decoder_2_out7),
    .out8(decoder_2_out8), .out9(decoder_2_out9), .out10(decoder_2_out10), .out11(decoder_2_out11),
    .out12(decoder_2_out12), .out13(decoder_2_out13), .out14(decoder_2_out14), .out15(decoder_2_out15),
    .out16(decoder_2_out16), .out17(decoder_2_out17), .out18(decoder_2_out18), .out19(decoder_2_out19),
    .out20(decoder_2_out20), .out21(decoder_2_out21), .out22(decoder_2_out22), .out23(decoder_2_out23),
    .out24(decoder_2_out24), .out25(decoder_2_out25), .out26(decoder_2_out26), .out27(decoder_2_out27),
    .out28(decoder_2_out28), .out29(decoder_2_out29), .out30(decoder_2_out30), .out31(decoder_2_out31),
    .sel(Rd), .en(or_4_out));
  Pull_Resistor pull_resistor_3 (.node(Rd_OUT));
  Pull_Resistor pull_resistor_4 (.node(Rr_OUT));
  Clock clock_1 (.out(clock_1_out));
  assign Rr_OUT = decoder_1_out0 ? register_1_q : 8'bz;  // Controlled_Buffer controlled_buffer_3
  assign controlled_buffer_4_out = decoder_2_out0 ? Rd_IN : 8'bz;  // Controlled_Buffer controlled_buffer_4
  Register register_1 (
    .D(controlled_buffer_4_out), .en(decoder_2_out0), .Q(register_1_q), .clk(clock_1_out));  // open: clr
  assign Rd_OUT = decoder_2_out0 ? register_1_q : 8'bz;  // Controlled_Buffer controlled_buffer_5
  assign Rr_OUT = decoder_1_out4 ? register_2_q : 8'bz;  // Controlled_Buffer controlled_buffer_6
  assign controlled_buffer_7_out = decoder_2_out4 ? Rd_IN : 8'bz;  // Controlled_Buffer controlled_buffer_7
  Register register_2 (
    .D(controlled_buffer_7_out), .en(decoder_2_out4), .Q(register_2_q), .clk(clock_1_out));  // open: clr
  assign Rd_OUT = decoder_2_out4 ? register_2_q : 8'bz;  // Controlled_Buffer controlled_buffer_8
  assign Rr_OUT = decoder_1_out8 ? register_3_q : 8'bz;  // Controlled_Buffer controlled_buffer_9
  Register register_3 (
    .D(controlled_buffer_10_out), .en(decoder_2_out8), .Q(register_3_q), .clk(clock_1_out));  // open: clr
  assign controlled_buffer_10_out = decoder_2_out8 ? Rd_IN : 8'bz;  // Controlled_Buffer controlled_buffer_10
  assign Rd_OUT = decoder_2_out8 ? register_3_q : 8'bz;  // Controlled_Buffer controlled_buffer_11
  assign Rr_OUT = decoder_1_out12 ? register_4_q : 8'bz;  // Controlled_Buffer controlled_buffer_12
  assign controlled_buffer_13_out = decoder_2_out12 ? Rd_IN : 8'bz;  // Controlled_Buffer controlled_buffer_13
  Register register_4 (
    .D(controlled_buffer_13_out), .en(decoder_2_out12), .Q(register_4_q), .clk(clock_1_out));  // open: clr
  assign Rd_OUT = decoder_2_out12 ? register_4_q : 8'bz;  // Controlled_Buffer controlled_buffer_14
  assign Rr_OUT = decoder_1_out16 ? register_5_q : 8'bz;  // Controlled_Buffer controlled_buffer_15
  assign controlled_buffer_16_out = decoder_2_out16 ? Rd_IN : 8'bz;  // Controlled_Buffer controlled_buffer_16
  Register register_5 (
    .D(controlled_buffer_16_out), .en(decoder_2_out16), .Q(register_5_q), .clk(clock_1_out));  // open: clr
  assign Rd_OUT = decoder_2_out16 ? register_5_q : 8'bz;  // Controlled_Buffer controlled_buffer_17
  assign Rr_OUT = decoder_1_out20 ? register_6_q : 8'bz;  // Controlled_Buffer controlled_buffer_18
  Register register_6 (
    .D(controlled_buffer_19_out), .en(decoder_2_out20), .Q(register_6_q), .clk(clock_1_out));  // open: clr
  assign controlled_buffer_19_out = decoder_2_out20 ? Rd_IN : 8'bz;  // Controlled_Buffer controlled_buffer_19
  assign Rd_OUT = decoder_2_out20 ? register_6_q : 8'bz;  // Controlled_Buffer controlled_buffer_20
  assign Rr_OUT = decoder_1_out24 ? register_7_q : 8'bz;  // Controlled_Buffer controlled_buffer_21
  Register register_7 (
    .D(controlled_buffer_22_out), .en(decoder_2_out24), .Q(register_7_q), .clk(clock_1_out));  // open: clr
  assign controlled_buffer_22_out = decoder_2_out24 ? Rd_IN : 8'bz;  // Controlled_Buffer controlled_buffer_22
  assign Rd_OUT = decoder_2_out24 ? register_7_q : 8'bz;  // Controlled_Buffer controlled_buffer_23
  assign Rr_OUT = decoder_1_out28 ? register_8_q : 8'bz;  // Controlled_Buffer controlled_buffer_24
  Register register_8 (
    .D(controlled_buffer_25_out), .en(decoder_2_out28), .Q(register_8_q), .clk(clock_1_out));  // open: clr
  assign controlled_buffer_25_out = decoder_2_out28 ? Rd_IN : 8'bz;  // Controlled_Buffer controlled_buffer_25
  assign Rd_OUT = decoder_2_out28 ? register_8_q : 8'bz;  // Controlled_Buffer controlled_buffer_26
  Register register_9 (
    .D(controlled_buffer_27_out), .en(decoder_2_out1), .Q(register_9_q), .clk(clock_1_out));  // open: clr
  assign controlled_buffer_27_out = decoder_2_out1 ? Rd_IN : 8'bz;  // Controlled_Buffer controlled_buffer_27
  assign controlled_buffer_28_out = decoder_2_out5 ? Rd_IN : 8'bz;  // Controlled_Buffer controlled_buffer_28
  Register register_10 (
    .D(controlled_buffer_28_out), .en(decoder_2_out5), .Q(register_10_q), .clk(clock_1_out));  // open: clr
  Register register_11 (
    .D(controlled_buffer_29_out), .en(decoder_2_out9), .Q(register_11_q), .clk(clock_1_out));  // open: clr
  assign controlled_buffer_29_out = decoder_2_out9 ? Rd_IN : 8'bz;  // Controlled_Buffer controlled_buffer_29
  assign controlled_buffer_30_out = decoder_2_out13 ? Rd_IN : 8'bz;  // Controlled_Buffer controlled_buffer_30
  Register register_12 (
    .D(controlled_buffer_30_out), .en(decoder_2_out13), .Q(register_12_q), .clk(clock_1_out));  // open: clr
  Register register_13 (
    .D(controlled_buffer_31_out), .en(decoder_2_out17), .Q(register_13_q), .clk(clock_1_out));  // open: clr
  assign controlled_buffer_31_out = decoder_2_out17 ? Rd_IN : 8'bz;  // Controlled_Buffer controlled_buffer_31
  Register register_14 (
    .D(controlled_buffer_32_out), .en(decoder_2_out21), .Q(register_14_q), .clk(clock_1_out));  // open: clr
  assign controlled_buffer_32_out = decoder_2_out21 ? Rd_IN : 8'bz;  // Controlled_Buffer controlled_buffer_32
  assign controlled_buffer_33_out = decoder_2_out25 ? Rd_IN : 8'bz;  // Controlled_Buffer controlled_buffer_33
  Register register_15 (
    .D(controlled_buffer_33_out), .en(decoder_2_out25), .Q(register_15_q), .clk(clock_1_out));  // open: clr
  Register register_16 (
    .D(controlled_buffer_34_out), .en(decoder_2_out29), .Q(register_16_q), .clk(clock_1_out));  // open: clr
  assign controlled_buffer_34_out = decoder_2_out29 ? Rd_IN : 8'bz;  // Controlled_Buffer controlled_buffer_34
  assign Rr_OUT = decoder_1_out1 ? register_9_q : 8'bz;  // Controlled_Buffer controlled_buffer_35
  assign controlled_buffer_36_out = decoder_2_out2 ? Rd_IN : 8'bz;  // Controlled_Buffer controlled_buffer_36
  assign Rd_OUT = decoder_2_out1 ? register_9_q : 8'bz;  // Controlled_Buffer controlled_buffer_37
  assign Rr_OUT = decoder_1_out5 ? register_10_q : 8'bz;  // Controlled_Buffer controlled_buffer_38
  assign controlled_buffer_39_out = decoder_2_out6 ? Rd_IN : 8'bz;  // Controlled_Buffer controlled_buffer_39
  assign Rd_OUT = decoder_2_out5 ? register_10_q : 8'bz;  // Controlled_Buffer controlled_buffer_40
  assign Rr_OUT = decoder_1_out9 ? register_11_q : 8'bz;  // Controlled_Buffer controlled_buffer_41
  assign controlled_buffer_42_out = decoder_2_out10 ? Rd_IN : 8'bz;  // Controlled_Buffer controlled_buffer_42
  assign Rd_OUT = decoder_2_out9 ? register_11_q : 8'bz;  // Controlled_Buffer controlled_buffer_43
  assign Rr_OUT = decoder_1_out13 ? register_12_q : 8'bz;  // Controlled_Buffer controlled_buffer_44
  assign controlled_buffer_45_out = decoder_2_out14 ? Rd_IN : 8'bz;  // Controlled_Buffer controlled_buffer_45
  assign Rd_OUT = decoder_2_out13 ? register_12_q : 8'bz;  // Controlled_Buffer controlled_buffer_46
  assign Rr_OUT = decoder_1_out17 ? register_13_q : 8'bz;  // Controlled_Buffer controlled_buffer_47
  assign controlled_buffer_48_out = decoder_2_out18 ? Rd_IN : 8'bz;  // Controlled_Buffer controlled_buffer_48
  assign Rd_OUT = decoder_2_out17 ? register_13_q : 8'bz;  // Controlled_Buffer controlled_buffer_49
  assign Rr_OUT = decoder_1_out21 ? register_14_q : 8'bz;  // Controlled_Buffer controlled_buffer_50
  assign controlled_buffer_51_out = decoder_2_out22 ? Rd_IN : 8'bz;  // Controlled_Buffer controlled_buffer_51
  assign Rd_OUT = decoder_2_out21 ? register_14_q : 8'bz;  // Controlled_Buffer controlled_buffer_52
  assign Rr_OUT = decoder_1_out25 ? register_15_q : 8'bz;  // Controlled_Buffer controlled_buffer_53
  assign controlled_buffer_54_out = decoder_2_out26 ? Rd_IN : 8'bz;  // Controlled_Buffer controlled_buffer_54
  assign Rd_OUT = decoder_2_out25 ? register_15_q : 8'bz;  // Controlled_Buffer controlled_buffer_55
  assign Rr_OUT = decoder_1_out29 ? register_16_q : 8'bz;  // Controlled_Buffer controlled_buffer_56
  assign controlled_buffer_57_out = decoder_2_out30 ? Rd_IN : 8'bz;  // Controlled_Buffer controlled_buffer_57
  assign Rd_OUT = decoder_2_out29 ? register_16_q : 8'bz;  // Controlled_Buffer controlled_buffer_58
  assign Rr_OUT = decoder_1_out2 ? register_17_q : 8'bz;  // Controlled_Buffer controlled_buffer_59
  Register register_17 (
    .D(controlled_buffer_36_out), .en(decoder_2_out2), .Q(register_17_q), .clk(clock_1_out));  // open: clr
  assign Rd_OUT = decoder_2_out2 ? register_17_q : 8'bz;  // Controlled_Buffer controlled_buffer_60
  assign Rr_OUT = decoder_1_out6 ? register_18_q : 8'bz;  // Controlled_Buffer controlled_buffer_61
  Register register_18 (
    .D(controlled_buffer_39_out), .en(decoder_2_out6), .Q(register_18_q), .clk(clock_1_out));  // open: clr
  assign Rd_OUT = decoder_2_out6 ? register_18_q : 8'bz;  // Controlled_Buffer controlled_buffer_62
  assign Rr_OUT = decoder_1_out10 ? register_19_q : 8'bz;  // Controlled_Buffer controlled_buffer_63
  Register register_19 (
    .D(controlled_buffer_42_out), .en(decoder_2_out10), .Q(register_19_q), .clk(clock_1_out));  // open: clr
  assign Rd_OUT = decoder_2_out10 ? register_19_q : 8'bz;  // Controlled_Buffer controlled_buffer_64
  assign Rr_OUT = decoder_1_out14 ? register_20_q : 8'bz;  // Controlled_Buffer controlled_buffer_65
  Register register_20 (
    .D(controlled_buffer_45_out), .en(decoder_2_out14), .Q(register_20_q), .clk(clock_1_out));  // open: clr
  assign Rd_OUT = decoder_2_out14 ? register_20_q : 8'bz;  // Controlled_Buffer controlled_buffer_66
  assign Rr_OUT = decoder_1_out18 ? register_21_q : 8'bz;  // Controlled_Buffer controlled_buffer_67
  Register register_21 (
    .D(controlled_buffer_48_out), .en(decoder_2_out18), .Q(register_21_q), .clk(clock_1_out));  // open: clr
  assign Rd_OUT = decoder_2_out18 ? register_21_q : 8'bz;  // Controlled_Buffer controlled_buffer_68
  assign Rr_OUT = decoder_1_out22 ? register_22_q : 8'bz;  // Controlled_Buffer controlled_buffer_69
  Register register_22 (
    .D(controlled_buffer_51_out), .en(decoder_2_out22), .Q(register_22_q), .clk(clock_1_out));  // open: clr
  assign Rd_OUT = decoder_2_out22 ? register_22_q : 8'bz;  // Controlled_Buffer controlled_buffer_70
  assign Rr_OUT = decoder_1_out26 ? register_23_q : 8'bz;  // Controlled_Buffer controlled_buffer_71
  Register register_23 (
    .D(controlled_buffer_54_out), .en(decoder_2_out26), .Q(register_23_q), .clk(clock_1_out));  // open: clr
  assign Rd_OUT = decoder_2_out26 ? register_23_q : 8'bz;  // Controlled_Buffer controlled_buffer_72
  assign Rr_OUT = decoder_1_out30 ? register_24_q : 8'bz;  // Controlled_Buffer controlled_buffer_73
  Register register_24 (
    .D(controlled_buffer_57_out), .en(decoder_2_out30), .Q(register_24_q), .clk(clock_1_out));  // open: clr
  assign Rd_OUT = decoder_2_out30 ? register_24_q : 8'bz;  // Controlled_Buffer controlled_buffer_74
  assign Rr_OUT = decoder_1_out3 ? register_25_q : 8'bz;  // Controlled_Buffer controlled_buffer_75
  Register register_25 (
    .D(controlled_buffer_76_out), .en(decoder_2_out3), .Q(register_25_q), .clk(clock_1_out));  // open: clr
  assign controlled_buffer_76_out = decoder_2_out3 ? Rd_IN : 8'bz;  // Controlled_Buffer controlled_buffer_76
  assign Rd_OUT = decoder_2_out3 ? register_25_q : 8'bz;  // Controlled_Buffer controlled_buffer_77
  assign Rr_OUT = decoder_1_out7 ? register_26_q : 8'bz;  // Controlled_Buffer controlled_buffer_78
  assign controlled_buffer_79_out = decoder_2_out7 ? Rd_IN : 8'bz;  // Controlled_Buffer controlled_buffer_79
  Register register_26 (
    .D(controlled_buffer_79_out), .en(decoder_2_out7), .Q(register_26_q), .clk(clock_1_out));  // open: clr
  assign Rd_OUT = decoder_2_out7 ? register_26_q : 8'bz;  // Controlled_Buffer controlled_buffer_80
  assign Rr_OUT = decoder_1_out11 ? register_27_q : 8'bz;  // Controlled_Buffer controlled_buffer_81
  Register register_27 (
    .D(controlled_buffer_82_out), .en(decoder_2_out11), .Q(register_27_q), .clk(clock_1_out));  // open: clr
  assign controlled_buffer_82_out = decoder_2_out11 ? Rd_IN : 8'bz;  // Controlled_Buffer controlled_buffer_82
  assign Rd_OUT = decoder_2_out11 ? register_27_q : 8'bz;  // Controlled_Buffer controlled_buffer_83
  assign Rr_OUT = decoder_1_out15 ? register_28_q : 8'bz;  // Controlled_Buffer controlled_buffer_84
  Register register_28 (
    .D(controlled_buffer_85_out), .en(decoder_2_out15), .Q(register_28_q), .clk(clock_1_out));  // open: clr
  assign controlled_buffer_85_out = decoder_2_out15 ? Rd_IN : 8'bz;  // Controlled_Buffer controlled_buffer_85
  assign Rd_OUT = decoder_2_out15 ? register_28_q : 8'bz;  // Controlled_Buffer controlled_buffer_86
  assign Rr_OUT = decoder_1_out19 ? register_29_q : 8'bz;  // Controlled_Buffer controlled_buffer_87
  assign controlled_buffer_88_out = decoder_2_out19 ? Rd_IN : 8'bz;  // Controlled_Buffer controlled_buffer_88
  Register register_29 (
    .D(controlled_buffer_88_out), .en(decoder_2_out19), .Q(register_29_q), .clk(clock_1_out));  // open: clr
  assign Rd_OUT = decoder_2_out19 ? register_29_q : 8'bz;  // Controlled_Buffer controlled_buffer_89
  assign Rr_OUT = decoder_1_out23 ? register_30_q : 8'bz;  // Controlled_Buffer controlled_buffer_90
  Register register_30 (
    .D(controlled_buffer_91_out), .en(decoder_2_out23), .Q(register_30_q), .clk(clock_1_out));  // open: clr
  assign controlled_buffer_91_out = decoder_2_out23 ? Rd_IN : 8'bz;  // Controlled_Buffer controlled_buffer_91
  assign Rd_OUT = decoder_2_out23 ? register_30_q : 8'bz;  // Controlled_Buffer controlled_buffer_92
  assign Rr_OUT = decoder_1_out27 ? register_31_q : 8'bz;  // Controlled_Buffer controlled_buffer_93
  Register register_31 (
    .D(controlled_buffer_94_out), .en(decoder_2_out27), .Q(register_31_q), .clk(clock_1_out));  // open: clr
  assign controlled_buffer_94_out = decoder_2_out27 ? Rd_IN : 8'bz;  // Controlled_Buffer controlled_buffer_94
  assign Rd_OUT = decoder_2_out27 ? register_31_q : 8'bz;  // Controlled_Buffer controlled_buffer_95
  assign Rr_OUT = decoder_1_out31 ? register_32_q : 8'bz;  // Controlled_Buffer controlled_buffer_96
  Register register_32 (
    .D(controlled_buffer_97_out), .en(decoder_2_out31), .Q(register_32_q), .clk(clock_1_out));  // open: clr
  assign controlled_buffer_97_out = decoder_2_out31 ? Rd_IN : 8'bz;  // Controlled_Buffer controlled_buffer_97
  assign Rd_OUT = decoder_2_out31 ? register_32_q : 8'bz;  // Controlled_Buffer controlled_buffer_98
endmodule

module FLASH (
  input  [15:0] PC_IN,
  input  [15:0] Indirect_IN,
  output [15:0] DATA_OUT
);

  wire clock_1_out;

  Clock clock_1 (.out(clock_1_out));
  RAM_part #(.addrWidth(16), .dataWidth(16), .bus("separate")) ram_1 (
    .addr(PC_IN), .din(Indirect_IN), .data(DATA_OUT), .str(1'b0), .clk(clock_1_out));  // open: sel, ld, clr
endmodule

// PC
module ProgCounter (
  input  [7:0] Addr_In,
  input  [15:0] Indirect_IN,
  input  LD_LO,
  input  LD_HI,
  input  PC_Enable,
  input  RESET,
  input  Indirect_Load,
  output [15:0] PC_OUT
);

  wire clock_1_out, or_2_out;
  wire [15:0] or_1_out, pull_resistor_1_node, pull_resistor_2_node, pull_resistor_3_node;

  Pull_Resistor pull_resistor_1 (.node(pull_resistor_1_node));
  assign pull_resistor_1_node = LD_LO ? {PC_OUT[15:8], Addr_In} : 16'bz;  // Controlled_Buffer controlled_buffer_1
  assign or_1_out = pull_resistor_1_node | pull_resistor_3_node | pull_resistor_2_node;  // OR_Gate or_1, 16 bits wide
  or or_2 (or_2_out, LD_LO, Indirect_Load, LD_HI);
  Pull_Resistor pull_resistor_2 (.node(pull_resistor_2_node));
  assign pull_resistor_2_node = LD_HI ? {Addr_In, PC_OUT[7:0]} : 16'bz;  // Controlled_Buffer controlled_buffer_2
  Counter #(.width(16), .max('hffff), .trigger("falling")) counter_1 (
    .load(or_2_out), .D(or_1_out), .count(PC_Enable), .Q(PC_OUT), .clk(clock_1_out), .clr(RESET));  // open: carry
  Clock clock_1 (.out(clock_1_out));
  Pull_Resistor pull_resistor_3 (.node(pull_resistor_3_node));
  assign pull_resistor_3_node = Indirect_Load ? Indirect_IN : 16'bz;  // Controlled_Buffer controlled_buffer_3
endmodule

// INSTRUCTION
module Instr_Reg (
  input  [15:0] in_1,
  input  Rd_16_31,
  input  Rd_0_31,
  input  Rr_0_31,
  input  Rd_24_26_28_30,
  input  Bits_hnb,
  input  Bits_lnb,
  input  Branch_Dest,
  input  Instr,
  input  IO_0_31,
  input  _8_Bit_Im,
  output [4:0] Rd_OUT,
  output [4:0] Rr_OUT,
  output [2:0] Bits_lnb_OUT,
  output [15:0] out_15,
  output [2:0] Bits_hnb_OUT,
  output [6:0] Rr_0_31_OUT,
  output [15:0] Instr_OUT,
  output [4:0] Rd_24_26_28_30_OUT,
  output [7:0] _8_Bit_Im_OUT
);

  wire clock_1_out, decoder_1_out0, decoder_1_out1, decoder_1_out2, decoder_1_out3;
  wire [4:0] adder_1_out, bit_extender_1_out, controlled_buffer_4_out;

  Clock clock_1 (.out(clock_1_out));
  Register #(.width(16), .trigger("high")) register_1 (.D(in_1), .Q(out_15), .clk(clock_1_out));  // open: en, clr
  Pull_Resistor pull_resistor_1 (.node(out_15[7:4]));
  assign bit_extender_1_out = {{1{1'b0}}, out_15[7:4]};  // Bit_Extender bit_extender_1
  Pull_Resistor pull_resistor_2 (.node(Rd_OUT));
  assign Rd_OUT = Rd_0_31 ? out_15[8:4] : 5'bz;  // Controlled_Buffer controlled_buffer_1
  Adder #(.width(5)) adder_1 (.a(bit_extender_1_out), .b(5'b10000), .out(adder_1_out));  // open: cin, cout
  assign Rd_OUT = Rd_16_31 ? adder_1_out : 5'bz;  // Controlled_Buffer controlled_buffer_2
  Pull_Resistor pull_resistor_3 (.node(Rd_OUT));
  assign Rr_OUT = Rr_0_31 ? {out_15[9], out_15[3:0]} : 5'bz;  // Controlled_Buffer controlled_buffer_3
  Pull_Resistor pull_resistor_4 (.node(Rr_OUT));
  Decoder_part #(.select(2), .disabled(0)) decoder_1 (
    .out0(decoder_1_out0), .out1(decoder_1_out1), .out2(decoder_1_out2), .out3(decoder_1_out3),
    .sel(out_15[5:4]), .en(Rd_24_26_28_30));
  assign controlled_buffer_4_out = decoder_1_out2 ? 5'b00100 : 5'bz;  // Controlled_Buffer controlled_buffer_4
  assign controlled_buffer_4_out = decoder_1_out3 ? 5'b00110 : 5'bz;  // Controlled_Buffer controlled_buffer_5
  assign controlled_buffer_4_out = decoder_1_out0 ? {5{1'b0}} : 5'bz;  // Controlled_Buffer controlled_buffer_6
  assign controlled_buffer_4_out = decoder_1_out1 ? 5'b00010 : 5'bz;  // Controlled_Buffer controlled_buffer_7
  assign Bits_hnb_OUT = Bits_hnb ? out_15[6:4] : 3'bz;  // Controlled_Buffer controlled_buffer_8
  Pull_Resistor pull_resistor_5 (.node(Rd_OUT));
  Adder #(.width(5)) adder_2 (.a(5'b11000), .b(controlled_buffer_4_out), .out(Rd_OUT));  // open: cin, cout
  assign Bits_lnb_OUT = Bits_lnb ? out_15[2:0] : 3'bz;  // Controlled_Buffer controlled_buffer_9
  Pull_Resistor pull_resistor_6 (.node(Bits_lnb_OUT));
  Pull_Resistor pull_resistor_7 (.node(Bits_hnb_OUT));
  Pull_Resistor pull_resistor_8 (.node(Rr_0_31_OUT));
  assign Rr_0_31_OUT = Branch_Dest ? out_15[9:3] : 7'bz;  // Controlled_Buffer controlled_buffer_10
  Pull_Resistor pull_resistor_9 (.node(Instr_OUT));
  assign Instr_OUT = Instr ? out_15 : 16'bz;  // Controlled_Buffer controlled_buffer_11
  Pull_Resistor pull_resistor_10 (.node(Rd_24_26_28_30_OUT));
  assign Rd_24_26_28_30_OUT = IO_0_31 ? out_15[7:3] : 5'bz;  // Controlled_Buffer controlled_buffer_12
  assign _8_Bit_Im_OUT = _8_Bit_Im ? {out_15[11:8], out_15[3:0]} : 8'bz;  // Controlled_Buffer controlled_buffer_13
  Pull_Resistor pull_resistor_11 (.node(_8_Bit_Im_OUT));
endmodule

// DEC
module Decoder (
  input  [15:0] in_1,
  output [31:0] CON1
);

  wire comparator_1_eq;

  Comparator #(.width(4), .mode("unsigned")) comparator_1 (
    .a(in_1[15:12]), .b(4'b1110), .eq(comparator_1_eq));  // open: gt, lt
  assign CON1[0] = comparator_1_eq ? 1'b1 : 1'bz;  // Controlled_Buffer controlled_buffer_1
  assign CON1[1] = comparator_1_eq ? 1'b1 : 1'bz;  // Controlled_Buffer controlled_buffer_2
  assign CON1[2] = comparator_1_eq ? 1'b1 : 1'bz;  // Controlled_Buffer controlled_buffer_3
  Pull_Resistor pull_resistor_1 (.node(CON1[2]));
  Pull_Resistor pull_resistor_2 (.node(CON1[1]));
  Pull_Resistor pull_resistor_3 (.node(CON1[0]));

  assign CON1[31:3] = {29{1'b0}};
endmodule
