// Logisim project AVR2.circ as structural Verilog: 6 circuits, main circuit AVRCore
module AVRCore (
);

  wire undriven, undriven_2;
  wire [15:0] flash_1_flash_out, instrreg_1_out, instrreg_1_to_dec;
  wire [31:0] decoder_1_ctrl_out;

  // Probe on undriven
  // Probe on undriven_2
  // Probe on instrreg_1_out
  InstrReg instrreg_1 (.Instr_IN(flash_1_flash_out), .TO_DEC(instrreg_1_to_dec), .OUT(instrreg_1_out));
  Flash flash_1 (.Flash_OUT(flash_1_flash_out));  // open: PC_IN
  Decoder decoder_1 (.Instr_IN(instrreg_1_to_dec), .Ctrl_OUT(decoder_1_ctrl_out));
  // Probe on decoder_1_ctrl_out
endmodule

// FLASH
module Flash (
  input  [15:0] PC_IN,
  output [15:0] Flash_OUT
);

  ROM #(.addrWidth(16), .dataWidth(16)) rom_1 (.addr(PC_IN), .data(Flash_OUT));  // open: sel
endmodule

// DEC
module Decoder (
  input  [15:0] Instr_IN,
  output [31:0] Ctrl_OUT
);

  wire clock_1_out, comparator_1_eq;
  wire [7:0] controlled_buffer_1_out;
  wire [15:0] register_1_q;

  Register #(.width(16)) register_1 (.D(Instr_IN), .en(Ctrl_OUT[0]), .Q(register_1_q), .clk(clock_1_out));  // open: clr
  Clock clock_1 (.out(clock_1_out));
  Comparator #(.width(16), .mode("unsigned")) comparator_1 (
    .a(register_1_q), .b({16{1'b0}}), .eq(comparator_1_eq));  // open: gt, lt
  assign controlled_buffer_1_out = comparator_1_eq ? {8{1'b0}} : 8'bz;  // Controlled_Buffer controlled_buffer_1
  ROM #(.dataWidth(32)) rom_1 (.addr(controlled_buffer_1_out), .data(Ctrl_OUT));  // open: sel
endmodule

// INSTR
module InstrReg (
  input  [15:0] Instr_IN,
  output [15:0] OUT,
  output [15:0] TO_DEC
);

  wire clock_1_out;

  Clock clock_1 (.out(clock_1_out));
  Register #(.width(16), .trigger("high")) register_1 (.D(Instr_IN), .Q(OUT), .clk(clock_1_out));  // open: en, clr

  assign TO_DEC = OUT;
endmodule

module ProgCounter (
  input  [31:0] Ctrl_IN,
  input  [15:0] Instr_IN,
  input  [7:0] Bus_1_IN,
  input  [7:0] Bus_2_IN,
  output [7:0] Bus_1_OUT,
  output [7:0] Bus_2_OUT,
  output [15:0] PC_2_OUT,
  output [15:0] PC_OUT
);

  wire B1O, B2O, clock_1_out;

  Clock clock_1 (.out(clock_1_out));
  Adder #(.width(16)) adder_1 (.a(PC_OUT), .b(16'h1), .out(PC_2_OUT));  // open: cin, cout
  Counter #(.width(16), .max('hffff)) counter_1 (
    .load(Ctrl_IN[1]), .count(Ctrl_IN[0]), .Q(PC_OUT), .clk(clock_1_out));  // open: D, carry, clr
  Pull_Resistor pull_resistor_1 (.node(Bus_1_OUT));
  Controlled_Buffer #(.width(8)) controlled_buffer_1 (.out(Bus_1_OUT), .en(B1O));  // open: in
  Pull_Resistor pull_resistor_2 (.node(B1O));
  Pull_Resistor pull_resistor_3 (.node(Bus_2_OUT));
  Controlled_Buffer #(.width(8)) controlled_buffer_2 (.out(Bus_2_OUT), .en(B2O));  // open: in
  Pull_Resistor pull_resistor_4 (.node(B2O));
endmodule

module Device (
  input  [31:0] Ctrl_IN,
  input  [15:0] Instr_IN,
  input  [7:0] Bus_1_IN,
  input  [7:0] Bus_2_IN,
  output [7:0] Bus_1_OUT,
  output [7:0] Bus_2_OUT
);

  wire B1O, B2O;

  Pull_Resistor pull_resistor_1 (.node(Bus_1_OUT));
  Controlled_Buffer #(.width(8)) controlled_buffer_1 (.out(Bus_1_OUT), .en(B1O));  // open: in
  Pull_Resistor pull_resistor_2 (.node(B1O));
  Pull_Resistor pull_resistor_3 (.node(Bus_2_OUT));
  Controlled_Buffer #(.width(8)) controlled_buffer_2 (.out(Bus_2_OUT), .en(B2O));  // open: in
  Pull_Resistor pull_resistor_4 (.node(B2O));
endmodule
